// Logisim project logisim-S2-T11.circ as structural Verilog: 4 circuits, main circuit main
module main (
  output Braille_Code,
  output out_2,
  output out_3,
  output out_4,
  output Space,
  output out_6,
  output out_7,
  output New_Line
);

  wire _1_out, _2_out, _4_out, _8_out, _16_out, A_out, B_out, C_out, clock_1_out, Counter_out, D_out,
       Delay_out, E_out, F_out, G_out, H_out, I_out, J_out, K_out, L_out, M_out, N_out, not_1_out, O_out,
       or_1_out, P_out, Q_out, R_out, S_out, SPACE_out, T_out, U_out, V_out, W_out, X_out, Y_out, Z_out;

  or _16 (_16_out, V_out, X_out, Z_out, S_out, T_out, Q_out, U_out, P_out, Y_out, R_out, W_out);
  Button Q (.out(Q_out));
  Button A (.out(A_out));
  Button W (.out(W_out));
  Button E (.out(E_out));
  Button S (.out(S_out));
  Button Z (.out(Z_out));
  Button X (.out(X_out));
  or _8 (_8_out, M_out, N_out, X_out, Z_out, L_out, K_out, J_out, H_out, O_out, I_out, Y_out);
  Button R (.out(R_out));
  Button D (.out(D_out));
  Button F (.out(F_out));
  Button C (.out(C_out));
  Converter converter_1 (
    .A(_16_out), .B(_8_out), .C(_4_out), .D(_2_out), .E(_1_out), .O1(Braille_Code), .O2(out_2), .O3(out_3),
    .O4(out_4), .O5(out_6), .O6(out_7));
  or _4 (_4_out, M_out, N_out, T_out, U_out, D_out, F_out, G_out, L_out, V_out, O_out, E_out, W_out);
  Button T (.out(T_out));
  Button G (.out(G_out));
  Button V (.out(V_out));
  Button u_SPACE (.out(SPACE_out));
  Button U (.out(U_out));
  Button Y (.out(Y_out));
  Button H (.out(H_out));
  Button B (.out(B_out));
  Button N (.out(N_out));
  or _2 (_2_out, N_out, B_out, V_out, J_out, Z_out, C_out, K_out, G_out, F_out, S_out, O_out, R_out, W_out);
  Button I (.out(I_out));
  Button K (.out(K_out));
  Button J (.out(J_out));
  Button M (.out(M_out));
  Button O (.out(O_out));
  Button L (.out(L_out));
  or _1 (_1_out, Q_out, W_out, E_out, Y_out, O_out, U_out, I_out, A_out, S_out, G_out, K_out, C_out, M_out);
  Button P (.out(P_out));
  or or_1 (or_1_out, Braille_Code, out_2, out_3, out_4, out_6, out_7, SPACE_out);
  Clock clock_1 (.out(clock_1_out));
  delay Delay (.clk(clock_1_out), .in(or_1_out), .out(Delay_out));
  Counter Counter (.in(or_1_out), .out(Counter_out));
  and and_1 (Space, Delay_out, not_1_out);
  not not_1 (not_1_out, Counter_out);
  and and_2 (New_Line, Delay_out, Counter_out);

  // Notes on the sheet:
  //   converter
  //   Keyboard
  //   Instructions:
  //   Text to Braile
  //   1.Press any button on keyboard
endmodule

module Converter (
  input  A,
  input  B,
  input  C,
  input  D,
  input  E,
  output O1,
  output O2,
  output O3,
  output O4,
  output O5,
  output O6
);

  wire and_1_out, and_2_out, and_3_out, and_4_out, and_5_out, and_6_out, and_7_out, and_8_out, and_9_out,
       and_10_out, and_11_out, and_12_out, and_13_out, and_14_out, and_15_out, and_16_out, and_17_out,
       and_18_out, and_19_out, and_20_out, and_21_out, and_22_out, and_23_out, and_24_out, and_25_out,
       and_26_out, and_27_out, and_28_out, and_29_out, and_30_out, and_31_out, and_32_out, and_33_out,
       and_34_out, not_1_out, not_2_out, not_3_out, not_4_out, not_5_out, not_6_out, not_7_out, not_8_out,
       not_9_out, not_10_out, not_11_out, not_12_out, not_13_out, not_14_out, not_15_out, not_16_out,
       not_17_out, not_18_out, not_19_out, not_20_out, not_21_out, not_22_out, not_23_out, not_24_out,
       not_25_out, not_26_out, not_27_out, not_28_out, not_29_out, not_30_out, not_31_out, not_32_out,
       not_33_out, not_34_out, not_35_out, not_36_out, not_37_out, not_38_out, not_39_out, not_40_out,
       not_41_out, not_42_out, not_43_out, not_44_out, not_45_out, not_46_out, not_47_out, not_48_out,
       not_49_out, not_50_out, not_51_out, not_52_out, not_53_out, not_54_out, not_55_out;

  not not_1 (not_1_out, B);
  not not_2 (not_2_out, D);
  not not_3 (not_3_out, B);
  not not_4 (not_4_out, E);
  not not_5 (not_5_out, A);
  not not_6 (not_6_out, A);
  not not_7 (not_7_out, A);
  not not_8 (not_8_out, D);
  not not_9 (not_9_out, E);
  not not_10 (not_10_out, C);
  not not_11 (not_11_out, D);
  not not_12 (not_12_out, C);
  not not_13 (not_13_out, E);
  not not_14 (not_14_out, B);
  not not_15 (not_15_out, A);
  not not_16 (not_16_out, B);
  not not_17 (not_17_out, E);
  not not_18 (not_18_out, D);
  not not_19 (not_19_out, A);
  not not_20 (not_20_out, E);
  not not_21 (not_21_out, C);
  not not_22 (not_22_out, D);
  not not_23 (not_23_out, D);
  not not_24 (not_24_out, E);
  not not_25 (not_25_out, A);
  not not_26 (not_26_out, C);
  not not_27 (not_27_out, E);
  not not_28 (not_28_out, B);
  not not_29 (not_29_out, A);
  not not_30 (not_30_out, C);
  not not_31 (not_31_out, D);
  not not_32 (not_32_out, A);
  not not_33 (not_33_out, D);
  not not_34 (not_34_out, E);
  not not_35 (not_35_out, B);
  not not_36 (not_36_out, C);
  not not_37 (not_37_out, B);
  not not_38 (not_38_out, E);
  not not_39 (not_39_out, A);
  not not_40 (not_40_out, B);
  not not_41 (not_41_out, D);
  not not_42 (not_42_out, B);
  not not_43 (not_43_out, D);
  not not_44 (not_44_out, E);
  not not_45 (not_45_out, A);
  not not_46 (not_46_out, C);
  not not_47 (not_47_out, E);
  not not_48 (not_48_out, E);
  not not_49 (not_49_out, C);
  not not_50 (not_50_out, D);
  not not_51 (not_51_out, C);
  not not_52 (not_52_out, E);
  not not_53 (not_53_out, C);
  not not_54 (not_54_out, D);
  not not_55 (not_55_out, E);
  and and_1 (and_1_out, A, C, E);
  and and_2 (and_2_out, A, C, D);
  and and_3 (and_3_out, A, B);
  and and_4 (and_4_out, not_1_out, not_2_out, E);
  and and_5 (and_5_out, not_3_out, D, not_4_out);
  and and_6 (and_6_out, not_5_out, D, E);
  and and_7 (and_7_out, not_6_out, C);
  and and_8 (and_8_out, not_7_out, B, not_8_out, not_9_out);
  and and_9 (and_9_out, A, not_10_out, not_11_out);
  and and_10 (and_10_out, A, not_12_out, not_13_out);
  and and_11 (and_11_out, not_14_out, D, E);
  and and_12 (and_12_out, not_15_out, not_16_out, C, not_17_out);
  and and_13 (and_13_out, B, not_18_out, E);
  and and_14 (and_14_out, not_19_out, B, D, not_20_out);
  and and_15 (and_15_out, A, not_21_out, not_22_out);
  and and_16 (and_16_out, A, not_23_out, not_24_out);
  and and_17 (and_17_out, not_25_out, not_26_out, D, not_27_out);
  and and_18 (and_18_out, not_28_out, C, D);
  and and_19 (and_19_out, not_29_out, B, not_30_out, not_31_out);
  and and_20 (and_20_out, not_32_out, B, not_33_out, not_34_out);
  and and_21 (and_21_out, A, not_35_out, not_36_out);
  and and_22 (and_22_out, A, not_37_out, not_38_out);
  and and_23 (and_23_out, not_39_out, not_40_out, C, not_41_out);
  and and_24 (and_24_out, not_42_out, C, not_43_out, not_44_out);
  and and_25 (and_25_out, C, D, E);
  and and_26 (and_26_out, not_45_out, B, not_46_out, not_47_out);
  and and_27 (and_27_out, B, D, not_48_out);
  and and_28 (and_28_out, A, not_49_out, not_50_out, E);
  and and_29 (and_29_out, A, not_51_out, D, not_52_out);
  and and_30 (and_30_out, B, D, E);
  and and_31 (and_31_out, B, C);
  and and_32 (and_32_out, A, not_53_out);
  and and_33 (and_33_out, A, not_54_out);
  and and_34 (and_34_out, A, not_55_out);
  or or_1 (O6, and_1_out, and_2_out, and_3_out);
  or or_2 (O1, and_4_out, and_5_out, and_6_out, and_7_out, and_8_out, and_9_out, and_10_out);
  or or_3 (O2, and_11_out, and_12_out, and_13_out, and_14_out, and_15_out, and_16_out);
  or or_4 (O3, and_17_out, and_18_out, and_19_out, and_20_out, and_21_out, and_22_out);
  or or_5 (O4, and_23_out, and_24_out, and_25_out, and_26_out, and_27_out, and_28_out, and_29_out);
  or or_6 (O5, and_30_out, and_31_out, and_32_out, and_33_out, and_34_out);
endmodule

module delay (
  input  clk,
  input  in,
  output out
);

  wire register_1_q;

  Register #(.width(1)) register_1 (.D(in), .Q(register_1_q), .clk(in), .clr(out));  // open: en
  D_Flip_Flop d_ff_1 (.clk(clk), .D(register_1_q), .Q(out));  // open: Qn, preset, en, reset
endmodule

module Counter (
  input  in,
  output out
);

  wire [3:0] counter_1_q;

  Counter_part #(.width(4), .max('hf)) counter_1 (
    .count(1'b1), .Q(counter_1_q), .clk(in));  // open: load, D, carry, clr
  nor nor_1 (out, counter_1_q[0], counter_1_q[1], counter_1_q[2], counter_1_q[3]);
endmodule
